// Logisim project Ejercicios_3.circ as structural Verilog
module Carro (
  input  Puerta1,
  input  Puerta3,
  input  Puerta2,
  input  Puerta4,
  input  Control,
  output out_6
);

  wire not_1_out, or_1_out;

  or or_1 (or_1_out, Puerta1, Puerta2, Puerta4, Puerta3);
  not not_1 (not_1_out, Control);
  and and_1 (out_6, or_1_out, not_1_out);
  LED Alarma (.in(out_6));
endmodule

module Sumador_1bit (
  input  A,
  input  B,
  input  Cin,
  output Suma,
  output Cout
);

  wire and_1_out, and_2_out, or_2_out, xor_1_out;

  xor xor_1 (xor_1_out, A, B);
  xor xor_2 (Suma, xor_1_out, Cin);
  or or_1 (Cout, and_1_out, and_2_out);
  and and_1 (and_1_out, A, B);
  or or_2 (or_2_out, A, B);
  and and_2 (and_2_out, or_2_out, Cin);
endmodule

module Sumador_4bits (
  input  A4,
  input  A3,
  input  A2,
  input  A1,
  input  B4,
  input  B3,
  input  B2,
  input  B1,
  input  CARRY,
  output out_10,
  output out_11,
  output out_12,
  output out_13,
  output out_14
);

  wire sumador_1bit_2_cout, sumador_1bit_3_cout, sumador_1bit_4_cout;

  Sumador_1bit sumador_1bit_1 (.A(A4), .B(B4), .Cin(sumador_1bit_2_cout), .Suma(out_11), .Cout(out_10));
  Sumador_1bit sumador_1bit_2 (.A(A3), .B(B3), .Cin(sumador_1bit_3_cout), .Suma(out_12), .Cout(sumador_1bit_2_cout));
  Sumador_1bit sumador_1bit_3 (.A(A2), .B(B2), .Cin(sumador_1bit_4_cout), .Suma(out_13), .Cout(sumador_1bit_3_cout));
  Sumador_1bit sumador_1bit_4 (.A(A1), .B(B1), .Cin(CARRY), .Suma(out_14), .Cout(sumador_1bit_4_cout));
endmodule

module Sumador_restador_4bits (
  input  B4,
  input  B3,
  input  B2,
  input  B1,
  input  A4,
  input  A3,
  input  A2,
  input  A1,
  input  S_R,
  output out_10,
  output out_11,
  output out_12,
  output out_13,
  output out_14
);

  wire sumador_1bit_2_cout, sumador_1bit_3_cout, sumador_1bit_4_cout, xor_1_out, xor_2_out, xor_3_out,
       xor_4_out;

  Sumador_1bit sumador_1bit_1 (.A(A4), .B(xor_1_out), .Cin(sumador_1bit_2_cout), .Suma(out_11), .Cout(out_10));
  Sumador_1bit sumador_1bit_2 (
    .A(A3), .B(xor_2_out), .Cin(sumador_1bit_3_cout), .Suma(out_12), .Cout(sumador_1bit_2_cout));
  xor xor_1 (xor_1_out, B4, S_R);
  Sumador_1bit sumador_1bit_3 (
    .A(A2), .B(xor_3_out), .Cin(sumador_1bit_4_cout), .Suma(out_13), .Cout(sumador_1bit_3_cout));
  xor xor_2 (xor_2_out, B3, S_R);
  Sumador_1bit sumador_1bit_4 (.A(A1), .B(xor_4_out), .Cin(S_R), .Suma(out_14), .Cout(sumador_1bit_4_cout));
  xor xor_3 (xor_3_out, B2, S_R);
  xor xor_4 (xor_4_out, B1, S_R);
endmodule

module multiplexador_1bit (
  input  Control,
  input  A,
  input  B,
  output out_4
);

  wire and_1_out, and_2_out, not_1_out;

  not not_1 (not_1_out, Control);
  and and_1 (and_1_out, not_1_out, A);
  and and_2 (and_2_out, Control, B);
  or or_1 (out_4, and_1_out, and_2_out);
endmodule

module multiplexador (
  input  sub,
  input  Cin,
  input  A,
  input  B,
  input  [2:0] OP,
  input  LESS,
  output Result,
  output Set,
  output Cout
);

  wire and_1_out, nor_1_out, or_1_out, xor_1_out, xor_2_out;

  xor xor_1 (xor_1_out, B, sub);
  and and_1 (and_1_out, A, B);
  or or_1 (or_1_out, A, B);
  xor xor_2 (xor_2_out, A, B);
  nor nor_1 (nor_1_out, A, B);
  Sumador_1bit sumador_1bit_1 (.A(A), .B(xor_1_out), .Cin(Cin), .Suma(Set), .Cout(Cout));
  Multiplexer #(.enable("true"), .select(3)) multiplexer_1 (
    .in0(and_1_out), .in1(or_1_out), .in2(xor_2_out), .in3(nor_1_out), .in4(Set), .in5(LESS), .out(Result),
    .sel(OP));  // open: in6, in7, en
endmodule

module ALU (
  input  Cin,
  input  [2:0] OP,
  input  [7:0] A,
  input  [7:0] B,
  output [7:0] Resultado,
  output Zero,
  output Overflow
);

  wire multiplexador_1_cout, multiplexador_2_cout, multiplexador_3_cout, multiplexador_4_cout,
       multiplexador_5_cout, multiplexador_6_cout, multiplexador_7_cout, multiplexador_8_set, not_1_out;

  multiplexador multiplexador_1 (
    .sub(Cin), .Cin(Cin), .A(A[0]), .B(B[0]), .OP(OP), .LESS(multiplexador_8_set), .Result(Resultado[0]),
    .Cout(multiplexador_1_cout));  // open: Set
  multiplexador multiplexador_2 (
    .sub(Cin), .Cin(multiplexador_1_cout), .A(A[1]), .B(B[1]), .OP(OP), .LESS(1'b0), .Result(Resultado[1]),
    .Cout(multiplexador_2_cout));  // open: Set
  multiplexador multiplexador_3 (
    .sub(Cin), .Cin(multiplexador_2_cout), .A(A[2]), .B(B[2]), .OP(OP), .LESS(1'b0), .Result(Resultado[2]),
    .Cout(multiplexador_3_cout));  // open: Set
  multiplexador multiplexador_4 (
    .sub(Cin), .Cin(multiplexador_3_cout), .A(A[3]), .B(B[3]), .OP(OP), .LESS(1'b0), .Result(Resultado[3]),
    .Cout(multiplexador_4_cout));  // open: Set
  multiplexador multiplexador_5 (
    .sub(Cin), .Cin(multiplexador_4_cout), .A(A[4]), .B(B[4]), .OP(OP), .LESS(1'b0), .Result(Resultado[4]),
    .Cout(multiplexador_5_cout));  // open: Set
  multiplexador multiplexador_6 (
    .sub(Cin), .Cin(multiplexador_5_cout), .A(A[5]), .B(B[5]), .OP(OP), .LESS(1'b0), .Result(Resultado[5]),
    .Cout(multiplexador_6_cout));  // open: Set
  multiplexador multiplexador_7 (
    .sub(Cin), .Cin(multiplexador_6_cout), .A(A[6]), .B(B[6]), .OP(OP), .LESS(1'b0), .Result(Resultado[6]),
    .Cout(multiplexador_7_cout));  // open: Set
  multiplexador multiplexador_8 (
    .sub(Cin), .Cin(multiplexador_7_cout), .A(A[7]), .B(B[7]), .OP(OP), .LESS(1'b0), .Result(Resultado[7]),
    .Set(multiplexador_8_set));  // open: Cout
  nor nor_1 (Zero, Resultado[0], Resultado[1], Resultado[2], Resultado[3], Resultado[4], Resultado[5], Resultado[6], Resultado[7]);
  not not_1 (not_1_out, Resultado[7]);
  and and_1 (Overflow, not_1_out, A[7], B[7]);
endmodule
